// Logisim project CRC.circ as structural Verilog: 2 circuits, main circuit CRC
module CRC (
  input  [7:0] in_1,
  input  [3:0] in_2,
  output [10:0] out_3
);

  wire [2:0] mod2_1_out_3, mod2_2_out_3, mod2_3_out_3, mod2_4_out_3, mod2_5_out_3, mod2_6_out_3, mod2_7_out_3;

  mod2 mod2_1 (.in_1(in_1[7:4]), .in_2(in_2), .out_3(mod2_1_out_3));  // open: out_4
  mod2 mod2_2 (.in_1({mod2_1_out_3, in_1[3]}), .in_2(in_2), .out_3(mod2_2_out_3));  // open: out_4
  mod2 mod2_3 (.in_1({mod2_2_out_3, in_1[2]}), .in_2(in_2), .out_3(mod2_3_out_3));  // open: out_4
  mod2 mod2_4 (.in_1({mod2_3_out_3, in_1[1]}), .in_2(in_2), .out_3(mod2_4_out_3));  // open: out_4
  mod2 mod2_5 (.in_1({mod2_4_out_3, in_1[0]}), .in_2(in_2), .out_3(mod2_5_out_3));  // open: out_4
  mod2 mod2_6 (.in_1({mod2_5_out_3, 1'b0}), .in_2(in_2), .out_3(mod2_6_out_3));  // open: out_4
  mod2 mod2_7 (.in_1({mod2_6_out_3, 1'b0}), .in_2(in_2), .out_3(mod2_7_out_3));  // open: out_4
  mod2 mod2_8 (.in_1({mod2_7_out_3, 1'b0}), .in_2(in_2), .out_3(out_3[2:0]));  // open: out_4

  assign out_3[10:3] = in_1;
endmodule

module mod2 (
  input  [3:0] in_1,
  input  [3:0] in_2,
  output [2:0] out_3,
  output out_4
);

  wire [3:0] multiplexer_1_out, xor_1_out;

  assign xor_1_out = in_1 ^ in_2;  // XOR_Gate xor_1, 4 bits wide
  Multiplexer #(.width(4)) multiplexer_1 (
    .in0(in_1), .in1(xor_1_out), .out(multiplexer_1_out), .sel(in_1[3]));  // open: en
  Bit_Extender #(.in_width(4), .out_width(3)) bit_extender_1 (.in(multiplexer_1_out), .out(out_3));

  assign out_4 = in_1[3];
endmodule
