// Logisim project fsm.circ as structural Verilog: 4 circuits, main circuit fsm
module fsm (
  input  clr,
  input  [1:0] in_2,
  output out_3
);

  wire clock_1_out, multiplexer_1_out, register_1_q;
  wire [1:0] save_1_out_4, shift_1_out_3;

  Register #(.width(1)) register_1 (
    .D(multiplexer_1_out), .Q(register_1_q), .clk(clock_1_out), .clr(register_1_q));  // open: en
  Multiplexer multiplexer_1 (.in0(1'b0), .in1(1'b1), .out(multiplexer_1_out), .sel(clr));  // open: en
  Clock clock_1 (.out(clock_1_out));
  shift shift_1 (.in(in_2), .prev(save_1_out_4), .out_3(shift_1_out_3));
  // Probe on shift_1_out_3
  // Probe on in_2
  save save_1 (.in_1(shift_1_out_3), .clk(clock_1_out), .rst(register_1_q), .out_4(save_1_out_4));
  // Probe on save_1_out_4
  ouput ouput_1 (.in_1(in_2), .in_2(save_1_out_4), .out_3(out_3));
endmodule

module shift (
  input  [1:0] in,
  input  [1:0] prev,
  output [1:0] out_3
);

  wire and_1_out, and_2_out, and_3_out, and_4_out, not_1_out, not_2_out, not_3_out, not_4_out, not_5_out,
       not_6_out, not_7_out;

  not not_1 (not_1_out, prev[1]);
  not not_2 (not_2_out, in[0]);
  not not_3 (not_3_out, prev[0]);
  not not_4 (not_4_out, in[0]);
  not not_5 (not_5_out, in[1]);
  not not_6 (not_6_out, prev[0]);
  not not_7 (not_7_out, in[0]);
  and and_1 (and_1_out, not_1_out, prev[0], not_2_out);
  and and_2 (and_2_out, prev[1], not_3_out, not_4_out);
  and and_3 (and_3_out, not_5_out, in[0]);
  and and_4 (and_4_out, prev[1], not_6_out, not_7_out);
  or or_1 (out_3[1], and_1_out, and_2_out);
  or or_2 (out_3[0], and_3_out, and_4_out);
endmodule

module save (
  input  [1:0] in_1,
  input  clk,
  input  rst,
  output [1:0] out_4
);

  Register #(.width(2)) register_1 (.D(in_1), .Q(out_4), .clk(clk), .clr(rst));  // open: en
endmodule

module ouput (
  input  [1:0] in_1,
  input  [1:0] in_2,
  output out_3
);

  wire bit_extender_1_out, comparator_1_eq, not_1_out;

  Bit_Extender #(.in_width(2), .out_width(1)) bit_extender_1 (.in(in_1), .out(bit_extender_1_out));
  Comparator #(.width(2), .mode("unsigned")) comparator_1 (.a(2'b10), .b(in_2), .eq(comparator_1_eq));  // open: gt, lt
  not not_1 (not_1_out, bit_extender_1_out);
  and and_1 (out_3, not_1_out, comparator_1_eq);
endmodule
