// Logisim project ftoi.circ as structural Verilog: 1 circuit, main circuit ftoi
module ftoi (
  input  [15:0] in_1,
  output [31:0] out_2
);

  wire and_1_out;
  wire [10:10] or_1_out;
  wire [11:0] bit_extender_1_out, multiplexer_1_out;
  wire [13:0] bit_extender_2_out, multiplexer_2_out;
  wire [17:0] bit_extender_3_out, multiplexer_3_out;
  wire [25:0] bit_extender_4_out, multiplexer_4_out;
  wire [31:0] adder_1_out, multiplexer_5_out, multiplexer_6_out, xor_1_out;

  or or_1 (or_1_out[10], in_1[10], in_1[11], in_1[12], in_1[13], in_1[14]);
  assign bit_extender_1_out = {{1{1'b0}}, {or_1_out[10], in_1[9:0]}};  // Bit_Extender bit_extender_1
  Multiplexer #(.width(12)) multiplexer_1 (
    .in0(bit_extender_1_out), .in1({or_1_out[10], in_1[9:0], 1'b0}), .out(multiplexer_1_out), .sel(in_1[10]));  // open: en
  assign bit_extender_2_out = {{2{1'b0}}, multiplexer_1_out};  // Bit_Extender bit_extender_2
  assign bit_extender_3_out = {{4{1'b0}}, multiplexer_2_out};  // Bit_Extender bit_extender_3
  Multiplexer #(.width(14)) multiplexer_2 (
    .in0(bit_extender_2_out), .in1({multiplexer_1_out, 2'b00}), .out(multiplexer_2_out), .sel(in_1[11]));  // open: en
  and and_1 (and_1_out, in_1[10], in_1[11], in_1[12], in_1[13], in_1[14]);
  Multiplexer #(.width(18)) multiplexer_3 (
    .in0(bit_extender_3_out), .in1({multiplexer_2_out, 4'b0000}), .out(multiplexer_3_out), .sel(in_1[12]));  // open: en
  assign bit_extender_4_out = {{8{1'b0}}, multiplexer_3_out};  // Bit_Extender bit_extender_4
  Multiplexer #(.width(26)) multiplexer_4 (
    .in0(bit_extender_4_out), .in1({multiplexer_3_out, {8{1'b0}}}), .out(multiplexer_4_out), .sel(in_1[13]));  // open: en
  Multiplexer #(.width(32)) multiplexer_5 (
    .in0({{31{1'b0}}, multiplexer_4_out[25]}), .in1({{15{1'b0}}, multiplexer_4_out[25:9]}),
    .out(multiplexer_5_out), .sel(in_1[14]));  // open: en
  assign xor_1_out = multiplexer_5_out ^ {32{1'b1}};  // XOR_Gate xor_1, 32 bits wide
  Adder #(.width(32)) adder_1 (.a(xor_1_out), .b(32'h1), .out(adder_1_out));  // open: cin, cout
  Multiplexer #(.width(32)) multiplexer_6 (
    .in0(multiplexer_5_out), .in1(adder_1_out), .out(multiplexer_6_out), .sel(in_1[15]));  // open: en
  Multiplexer #(.width(32)) multiplexer_7 (
    .in0(multiplexer_6_out), .in1({32{1'b0}}), .out(out_2), .sel(and_1_out));  // open: en

  // Other names for the same wires on the sheet: s = in_1[15]
endmodule
