// Logisim project grf.circ as structural Verilog: 2 circuits, main circuit grf
module grf (
  input  [4:0] A1,
  input  [4:0] A2,
  input  in_3,
  input  in_4,
  input  in_5,
  input  [4:0] A3,
  input  [31:0] WD,
  output [31:0] out_8,
  output [31:0] out_9
);

  wire r10, r11, r12, r13, r14, r15, r16, r17, r18, r19, r20, r21, r22, r23, r24, r25, r26, r27, r28, r29,
       r30, r31, r32, r33, r34, r35, r36, r37, r38, r39, r110, r111, r112, r113, r114, r115, r116, r117,
       r118, r119, r120, r121, r122, r123, r124, r125, r126, r127, r128, r129, r130, r131, r210, r211, r212,
       r213, r214, r215, r216, r217, r218, r219, r220, r221, r222, r223, r224, r225, r226, r227, r228, r229,
       r230, r231, r310, r311, r312, r313, r314, r315, r316, r317, r318, r319, r320, r321, r322, r323, r324,
       r325, r326, r327, r328, r329, r330, r331;
  wire [31:0] o11, o12, o13, o14, o15, o16, o17, o18, o19, o21, o22, o23, o24, o25, o26, o27, o28, o29, o110,
       o111, o112, o113, o114, o115, o116, o117, o118, o119, o120, o121, o122, o123, o124, o125, o126, o127,
       o128, o129, o130, o131, o210, o211, o212, o213, o214, o215, o216, o217, o218, o219, o220, o221, o222,
       o223, o224, o225, o226, o227, o228, o229, o230, o231;

  Decoder #(.select(5), .disabled(0), .enable("false")) decoder_1 (
    .out0(r10), .out1(r11), .out2(r12), .out3(r13), .out4(r14), .out5(r15), .out6(r16), .out7(r17),
    .out8(r18), .out9(r19), .out10(r110), .out11(r111), .out12(r112), .out13(r113), .out14(r114),
    .out15(r115), .out16(r116), .out17(r117), .out18(r118), .out19(r119), .out20(r120), .out21(r121),
    .out22(r122), .out23(r123), .out24(r124), .out25(r125), .out26(r126), .out27(r127), .out28(r128),
    .out29(r129), .out30(r130), .out31(r131), .sel(A1));
  Decoder #(.select(5), .disabled(0), .enable("false")) decoder_2 (
    .out0(r20), .out1(r21), .out2(r22), .out3(r23), .out4(r24), .out5(r25), .out6(r26), .out7(r27),
    .out8(r28), .out9(r29), .out10(r210), .out11(r211), .out12(r212), .out13(r213), .out14(r214),
    .out15(r215), .out16(r216), .out17(r217), .out18(r218), .out19(r219), .out20(r220), .out21(r221),
    .out22(r222), .out23(r223), .out24(r224), .out25(r225), .out26(r226), .out27(r227), .out28(r228),
    .out29(r229), .out30(r230), .out31(r231), .sel(A2));
  Decoder #(.select(5), .disabled(0), .enable("false")) decoder_3 (
    .out0(r30), .out1(r31), .out2(r32), .out3(r33), .out4(r34), .out5(r35), .out6(r36), .out7(r37),
    .out8(r38), .out9(r39), .out10(r310), .out11(r311), .out12(r312), .out13(r313), .out14(r314),
    .out15(r315), .out16(r316), .out17(r317), .out18(r318), .out19(r319), .out20(r320), .out21(r321),
    .out22(r322), .out23(r323), .out24(r324), .out25(r325), .out26(r326), .out27(r327), .out28(r328),
    .out29(r329), .out30(r330), .out31(r331), .sel(A3));
  Multiplexer #(.select(5), .width(32), .disabled(0), .enable("false")) multiplexer_1 (
    .in0({32{1'b0}}), .in1(o11), .in2(o12), .in3(o13), .in4(o14), .in5(o15), .in6(o16), .in7(o17), .in8(o18),
    .in9(o19), .in10(o110), .in11(o111), .in12(o112), .in13(o113), .in14(o114), .in15(o115), .in16(o116),
    .in17(o117), .in18(o118), .in19(o119), .in20(o120), .in21(o121), .in22(o122), .in23(o123), .in24(o124),
    .in25(o125), .in26(o126), .in27(o127), .in28(o128), .in29(o129), .in30(o130), .in31(o131), .out(out_8),
    .sel(A1));
  Multiplexer #(.select(5), .width(32), .disabled(0), .enable("false")) multiplexer_2 (
    .in0({32{1'b0}}), .in1(o21), .in2(o22), .in3(o23), .in4(o24), .in5(o25), .in6(o26), .in7(o27), .in8(o28),
    .in9(o29), .in10(o210), .in11(o211), .in12(o212), .in13(o213), .in14(o214), .in15(o215), .in16(o216),
    .in17(o217), .in18(o218), .in19(o219), .in20(o220), .in21(o221), .in22(o222), .in23(o223), .in24(o224),
    .in25(o225), .in26(o226), .in27(o227), .in28(o228), .in29(o229), .in30(o230), .in31(o231), .out(out_9),
    .sel(A2));
  unit unit_1 (.\input (WD), .c(in_3), .o1(o14), .o2(o24), .a3(r34), .we(in_5), .r(in_4), .in_5(r14), .in_6(r24));
  unit unit_2 (.\input (WD), .c(in_3), .o1(o18), .o2(o28), .a3(r38), .we(in_5), .r(in_4), .in_5(r18), .in_6(r28));
  unit unit_3 (.\input (WD), .c(in_3), .o1(o112), .o2(o212), .a3(r312), .we(in_5), .r(in_4), .in_5(r112), .in_6(r212));
  unit unit_4 (.\input (WD), .c(in_3), .o1(o116), .o2(o216), .a3(r316), .we(in_5), .r(in_4), .in_5(r116), .in_6(r216));
  unit unit_5 (.\input (WD), .c(in_3), .o1(o120), .o2(o220), .a3(r320), .we(in_5), .r(in_4), .in_5(r120), .in_6(r220));
  unit unit_6 (.\input (WD), .c(in_3), .o1(o124), .o2(o224), .a3(r324), .we(in_5), .r(in_4), .in_5(r124), .in_6(r224));
  unit unit_7 (.\input (WD), .c(in_3), .o1(o128), .o2(o228), .a3(r328), .we(in_5), .r(in_4), .in_5(r128), .in_6(r228));
  unit unit_8 (.\input (WD), .c(in_3), .o1(o11), .o2(o21), .a3(r31), .we(in_5), .r(in_4), .in_5(r11), .in_6(r21));
  unit unit_9 (.\input (WD), .c(in_3), .o1(o15), .o2(o25), .a3(r35), .we(in_5), .r(in_4), .in_5(r15), .in_6(r25));
  unit unit_10 (.\input (WD), .c(in_3), .o1(o19), .o2(o29), .a3(r39), .we(in_5), .r(in_4), .in_5(r19), .in_6(r29));
  unit unit_11 (.\input (WD), .c(in_3), .o1(o113), .o2(o213), .a3(r313), .we(in_5), .r(in_4), .in_5(r113), .in_6(r213));
  unit unit_12 (.\input (WD), .c(in_3), .o1(o117), .o2(o217), .a3(r317), .we(in_5), .r(in_4), .in_5(r117), .in_6(r217));
  unit unit_13 (.\input (WD), .c(in_3), .o1(o121), .o2(o221), .a3(r321), .we(in_5), .r(in_4), .in_5(r121), .in_6(r221));
  unit unit_14 (.\input (WD), .c(in_3), .o1(o125), .o2(o225), .a3(r325), .we(in_5), .r(in_4), .in_5(r125), .in_6(r225));
  unit unit_15 (.\input (WD), .c(in_3), .o1(o129), .o2(o229), .a3(r329), .we(in_5), .r(in_4), .in_5(r129), .in_6(r229));
  unit unit_16 (.\input (WD), .c(in_3), .o1(o12), .o2(o22), .a3(r32), .we(in_5), .r(in_4), .in_5(r12), .in_6(r22));
  unit unit_17 (.\input (WD), .c(in_3), .o1(o16), .o2(o26), .a3(r36), .we(in_5), .r(in_4), .in_5(r16), .in_6(r26));
  unit unit_18 (.\input (WD), .c(in_3), .o1(o110), .o2(o210), .a3(r310), .we(in_5), .r(in_4), .in_5(r110), .in_6(r210));
  unit unit_19 (.\input (WD), .c(in_3), .o1(o114), .o2(o214), .a3(r314), .we(in_5), .r(in_4), .in_5(r114), .in_6(r214));
  unit unit_20 (.\input (WD), .c(in_3), .o1(o118), .o2(o218), .a3(r318), .we(in_5), .r(in_4), .in_5(r118), .in_6(r218));
  unit unit_21 (.\input (WD), .c(in_3), .o1(o122), .o2(o222), .a3(r322), .we(in_5), .r(in_4), .in_5(r122), .in_6(r222));
  unit unit_22 (.\input (WD), .c(in_3), .o1(o126), .o2(o226), .a3(r326), .we(in_5), .r(in_4), .in_5(r126), .in_6(r226));
  unit unit_23 (.\input (WD), .c(in_3), .o1(o130), .o2(o230), .a3(r330), .we(in_5), .r(in_4), .in_5(r130), .in_6(r230));
  unit unit_24 (.\input (WD), .c(in_3), .o1(o13), .o2(o23), .a3(r33), .we(in_5), .r(in_4), .in_5(r13), .in_6(r23));
  unit unit_25 (.\input (WD), .c(in_3), .o1(o17), .o2(o27), .a3(r37), .we(in_5), .r(in_4), .in_5(r17), .in_6(r27));
  unit unit_26 (.\input (WD), .c(in_3), .o1(o111), .o2(o211), .a3(r311), .we(in_5), .r(in_4), .in_5(r111), .in_6(r211));
  unit unit_27 (.\input (WD), .c(in_3), .o1(o115), .o2(o215), .a3(r315), .we(in_5), .r(in_4), .in_5(r115), .in_6(r215));
  unit unit_28 (.\input (WD), .c(in_3), .o1(o119), .o2(o219), .a3(r319), .we(in_5), .r(in_4), .in_5(r119), .in_6(r219));
  unit unit_29 (.\input (WD), .c(in_3), .o1(o123), .o2(o223), .a3(r323), .we(in_5), .r(in_4), .in_5(r123), .in_6(r223));
  unit unit_30 (.\input (WD), .c(in_3), .o1(o127), .o2(o227), .a3(r327), .we(in_5), .r(in_4), .in_5(r127), .in_6(r227));
  unit unit_31 (.\input (WD), .c(in_3), .o1(o131), .o2(o231), .a3(r331), .we(in_5), .r(in_4), .in_5(r131), .in_6(r231));

  // Other names for the same wires on the sheet: clk = in_3; reset = in_4; WE = in_5
endmodule

module unit (
  input  [31:0] \input ,
  input  a3,
  input  we,
  input  r,
  input  in_5,
  input  in_6,
  input  c,
  output [31:0] o1,
  output [31:0] o2
);

  wire [31:0] multiplexer_1_out, register_1_q;

  Multiplexer #(.width(32), .disabled(0), .enable("false")) multiplexer_1 (
    .in0(register_1_q), .in1(\input ), .out(multiplexer_1_out), .sel(a3));
  Register #(.width(32)) register_1 (.D(multiplexer_1_out), .en(we), .Q(register_1_q), .clk(c), .clr(r));
  Multiplexer #(.width(32), .disabled(0), .enable("false")) multiplexer_2 (
    .in1(register_1_q), .out(o1), .sel(in_5));  // open: in0
  Multiplexer #(.width(32), .disabled(0), .enable("false")) multiplexer_3 (
    .in1(register_1_q), .out(o2), .sel(in_6));  // open: in0
endmodule
