// Logisim project P3.circ as structural Verilog: 8 circuits, main circuit main
module main (
  input  Rst,
  output [31:0] out_2,
  output out_3,
  output [4:0] out_4,
  output [31:0] out_5,
  output out_6,
  output [4:0] out_7,
  output [31:0] out_8
);

  wire ALU_zero, b_eq_out, Clk, Controller_alusrc, Controller_branch, Controller_memread,
       Controller_memtoreg, Controller_regdest;
  wire [2:0] ALUOp;
  wire [3:0] alucontrol_1_aluoperation;
  wire [31:0] adder_1_out, ALU_result, bit_extender_1_out, DM_readdata, IFU_pcplus, multiplexer_1_out,
       multiplexer_3_out, Register_readdata1, shifter_1_out;

  Multiplexer #(.width(32), .enable("false")) multiplexer_1 (
    .in0(IFU_pcplus), .in1(adder_1_out), .out(multiplexer_1_out), .sel(b_eq_out));
  IFU IFU (.PCNext(multiplexer_1_out), .C(Clk), .R(Rst), .Instruction(out_2), .PCPlus(IFU_pcplus));
  Controller Controller (
    .OpCode(out_2[31:26]), .Funct(out_2[5:0]), .RegDest(Controller_regdest), .ALUSrc(Controller_alusrc),
    .MemtoReg(Controller_memtoreg), .RegWrite(out_3), .MemRead(Controller_memread), .MemWrite(out_6),
    .Branch(Controller_branch), .ALUOp2_I(ALUOp[2]), .ALUOp1_R(ALUOp[1]), .ALUOp0_J(ALUOp[0]));
  Multiplexer #(.width(5), .enable("false")) multiplexer_2 (
    .in0(out_2[20:16]), .in1(out_2[15:11]), .out(out_4), .sel(Controller_regdest));
  assign bit_extender_1_out = {{16{1'b0}}, out_2[15:0]};  // Bit_Extender bit_extender_1
  Clock clock_1 (.out(Clk));
  Registers Register (
    .A1(out_2[25:21]), .A2(out_2[20:16]), .WriteRegister(out_4), .WD(out_5), .in_4(Clk), .in_5(out_3),
    .in_3(Rst), .ReadData1(Register_readdata1), .ReadData2(out_8));
  Shifter #(.width(32)) shifter_1 (.in(bit_extender_1_out), .\dist (5'b00010), .out(shifter_1_out));
  Multiplexer #(.width(32), .enable("false")) multiplexer_3 (
    .in0(out_8), .in1(bit_extender_1_out), .out(multiplexer_3_out), .sel(Controller_alusrc));
  Adder #(.width(32)) adder_1 (.a(shifter_1_out), .b(IFU_pcplus), .out(adder_1_out));  // open: cin, cout
  and b_eq (b_eq_out, Controller_branch, ALU_zero);
  ALU ALU (
    .A(Register_readdata1), .B(multiplexer_3_out), .Op(alucontrol_1_aluoperation),
    .Result({ALU_result[31:7], out_7, ALU_result[1:0]}), .Zero(ALU_zero));
  ALUControl alucontrol_1 (
    .ALUOp(ALUOp), .OpCode(out_2[31:26]), .Funct(out_2[5:0]), .ALUOperation(alucontrol_1_aluoperation));
  DM DM (
    .Addr(out_7), .WriteData(out_8), .MemRead(Controller_memread), .MemWrite(out_6), .Clk(Clk),
    .ReadData(DM_readdata));
  Multiplexer #(.width(32), .enable("false")) multiplexer_4 (
    .in0({ALU_result[31:7], out_7, ALU_result[1:0]}), .in1(DM_readdata), .out(out_5),
    .sel(Controller_memtoreg));

  // Other names for the same wires on the sheet: MemAddr[4:0] = out_7; Instruction[31:0] = out_2;
  //   MemData[31:0] = out_8; MemWrite = out_6; RegAddr[4:0] = out_4; RegData[31:0] = out_5; RegWrite = out_3
endmodule

module Controller (
  input  [5:0] OpCode,
  input  [5:0] Funct,
  output RegDest,
  output ALUSrc,
  output MemtoReg,
  output RegWrite,
  output MemRead,
  output MemWrite,
  output Branch,
  output ALUOp2_I,
  output ALUOp1_R,
  output ALUOp0_J
);

  wire add_out, add_sub_out, lui_out, not_1_out, not_2_out, not_3_out, not_4_out, not_5_out, not_6_out,
       not_7_out, not_8_out, not_9_out, not_10_out, not_11_out, not_12_out, ori_out, sub_out;

  not not_1 (not_1_out, OpCode[5]);
  not not_2 (not_2_out, OpCode[4]);
  not not_3 (not_3_out, OpCode[3]);
  not not_4 (not_4_out, OpCode[2]);
  not not_5 (not_5_out, OpCode[1]);
  not not_6 (not_6_out, OpCode[0]);
  and add_sub (add_sub_out, not_1_out, not_2_out, not_3_out, not_4_out, not_5_out, not_6_out);
  and ori (ori_out, not_1_out, not_2_out, OpCode[3], OpCode[2], not_5_out, OpCode[0]);
  and lw (MemRead, OpCode[5], not_2_out, not_3_out, not_4_out, OpCode[1], OpCode[0]);
  and sw (MemWrite, OpCode[5], not_2_out, OpCode[3], not_4_out, OpCode[1], OpCode[0]);
  and beq (ALUOp0_J, not_1_out, not_2_out, not_3_out, OpCode[2], not_5_out, not_6_out);
  and lui (lui_out, not_1_out, not_2_out, OpCode[3], OpCode[2], OpCode[1], OpCode[0]);
  not not_7 (not_7_out, Funct[4]);
  not not_8 (not_8_out, Funct[3]);
  not not_9 (not_9_out, Funct[5]);
  or or_1 (RegDest, 1'b0, add_sub_out);
  or or_2 (ALUSrc, MemRead, lui_out, ori_out, MemWrite);
  not not_10 (not_10_out, Funct[1]);
  not not_11 (not_11_out, Funct[0]);
  not not_12 (not_12_out, Funct[2]);
  and add (add_out, Funct[5], not_7_out, not_8_out, add_sub_out, not_12_out, not_10_out, not_11_out);
  and sub (sub_out, Funct[5], not_7_out, not_8_out, add_sub_out, not_12_out, Funct[1], not_11_out);
  or or_3 (RegWrite, MemRead, lui_out, ori_out, add_sub_out);
  or or_4 (ALUOp2_I, lui_out, ori_out);
  or or_5 (ALUOp1_R, 1'b0, add_sub_out);

  assign Branch = ALUOp0_J;
  assign MemtoReg = MemRead;
endmodule

module ALUControl (
  input  [2:0] ALUOp,
  input  [5:0] OpCode,
  input  [5:0] Funct,
  output [3:0] ALUOperation
);

  wire addu_2_out, addu_out, and_2_out, and_out, comparator_1_eq, comparator_2_eq, comparator_3_eq, I,
       lui_2_out, lui_out, not_1_out, not_2_out, not_3_out, not_4_out, not_5_out, not_6_out, not_7_out,
       not_8_out, not_9_out, not_10_out, not_11_out, not_12_out, or_2_out, or_3_out, or_4_out, or_out,
       ori_2_out, ori_out, subu_2_out, subu_out;
  wire [3:0] FuncResult, multiplexer_1_out, multiplexer_2_out, multiplexer_3_out, multiplexer_4_out,
       multiplexer_5_out, multiplexer_6_out, OpResult;

  not not_1 (not_1_out, Funct[3]);
  not not_2 (not_2_out, Funct[4]);
  not not_3 (not_3_out, Funct[5]);
  not not_4 (not_4_out, Funct[1]);
  not not_5 (not_5_out, Funct[0]);
  not not_6 (not_6_out, Funct[2]);
  and addu (addu_out, Funct[5], not_2_out, not_1_out, not_6_out, not_4_out, Funct[0]);
  and subu (subu_out, Funct[5], not_2_out, not_1_out, not_6_out, Funct[1], Funct[0]);
  and \and  (and_out, Funct[5], not_2_out, not_1_out, Funct[2], not_4_out, not_5_out);
  and \or  (or_out, Funct[5], not_2_out, not_1_out, Funct[2], not_4_out, Funct[0]);
  Comparator #(.width(3), .mode("unsigned")) comparator_1 (
    .a(ALUOp), .b(3'b000), .eq(comparator_1_eq));  // open: gt, lt
  Comparator #(.width(3), .mode("unsigned")) comparator_2 (
    .a(ALUOp), .b(3'b001), .eq(comparator_2_eq));  // open: gt, lt
  Comparator #(.width(3), .mode("unsigned")) comparator_3 (
    .a(ALUOp), .b(3'b010), .eq(comparator_3_eq));  // open: gt, lt
  Comparator #(.width(3), .mode("unsigned")) comparator_4 (.a(ALUOp), .b(3'b100), .eq(I));  // open: gt, lt
  and addu_2 (addu_2_out, comparator_3_eq, addu_out);
  and subu_2 (subu_2_out, comparator_3_eq, subu_out);
  and and_2 (and_2_out, comparator_3_eq, and_out);
  and or_2 (or_2_out, comparator_3_eq, or_out);
  Multiplexer #(.width(4), .enable("false")) multiplexer_1 (
    .in0(4'b0000), .in1(4'b0010), .out(multiplexer_1_out), .sel(or_3_out));
  or or_3 (or_3_out, comparator_1_eq, addu_2_out);
  Multiplexer #(.width(4), .enable("false")) multiplexer_2 (
    .in0(4'b0000), .in1(4'b0110), .out(multiplexer_2_out), .sel(or_4_out));
  or or_4 (or_4_out, comparator_2_eq, subu_2_out);
  Multiplexer #(.width(4), .enable("false")) multiplexer_3 (
    .in0(4'b0000), .in1(4'b0000), .out(multiplexer_3_out), .sel(and_2_out));
  Multiplexer #(.width(4), .enable("false")) multiplexer_4 (
    .in0(4'b0000), .in1(4'b0001), .out(multiplexer_4_out), .sel(or_2_out));
  assign ALUOperation = FuncResult | OpResult;  // OR_Gate or_5, 4 bits wide
  assign FuncResult = multiplexer_1_out | multiplexer_2_out | multiplexer_3_out | multiplexer_4_out;  // OR_Gate or_6, 4 bits wide
  not not_7 (not_7_out, OpCode[3]);
  not not_8 (not_8_out, OpCode[4]);
  not not_9 (not_9_out, OpCode[5]);
  not not_10 (not_10_out, OpCode[1]);
  not not_11 (not_11_out, OpCode[2]);
  not not_12 (not_12_out, OpCode[0]);
  and ori (ori_out, not_9_out, not_8_out, OpCode[3], OpCode[2], not_10_out, OpCode[0]);
  and lui (lui_out, not_9_out, not_8_out, OpCode[3], OpCode[2], OpCode[1], OpCode[0]);
  Multiplexer #(.width(4), .enable("false")) multiplexer_5 (
    .in0(4'b0000), .in1(4'b0001), .out(multiplexer_5_out), .sel(ori_2_out));
  and ori_2 (ori_2_out, I, ori_out);
  Multiplexer #(.width(4), .enable("false")) multiplexer_6 (
    .in0(4'b0000), .in1(4'b1000), .out(multiplexer_6_out), .sel(lui_2_out));
  and lui_2 (lui_2_out, I, lui_out);
  assign OpResult = multiplexer_5_out | multiplexer_6_out;  // OR_Gate or_7, 4 bits wide
endmodule

module IFU (
  input  [31:0] PCNext,
  input  C,
  input  R,
  output [31:0] Instruction,
  output [31:0] PCPlus
);

  wire [31:0] PC_q;

  Register #(.width(32)) PC (.D(PCNext), .Q(PC_q), .clk(C), .clr(R));  // open: en
  Adder #(.width(32)) adder_1 (.a(PC_q), .b(32'h4), .out(PCPlus));  // open: cin, cout
  ROM #(.addrWidth(5), .dataWidth(32)) rom_1 (.addr(PC_q[6:2]), .data(Instruction));  // open: sel

  // Notes on the sheet:
  //   contents of rom_1 (hex, n*v repeats v):
  //   350800ff 35290001 1094023
endmodule

module DM (
  input  MemRead,
  input  MemWrite,
  input  [4:0] Addr,
  input  [31:0] WriteData,
  input  Clk,
  output [31:0] ReadData
);

  wire not_1_out;

  not not_1 (not_1_out, Clk);
  RAM #(.addrWidth(5), .dataWidth(32), .bus("separate")) ram_1 (
    .addr(Addr), .din(WriteData), .data(ReadData), .str(MemWrite), .clk(not_1_out), .ld(MemRead));  // open: sel, clr
endmodule

module Registers (
  input  [4:0] A1,
  input  [4:0] A2,
  input  in_3,
  input  in_4,
  input  in_5,
  input  [4:0] WriteRegister,
  input  [31:0] WD,
  output [31:0] ReadData1,
  output [31:0] ReadData2
);

  wire r10, r11, r12, r13, r14, r15, r16, r17, r18, r19, r20, r21, r22, r23, r24, r25, r26, r27, r28, r29,
       r30, r31, r32, r33, r34, r35, r36, r37, r38, r39, r110, r111, r112, r113, r114, r115, r116, r117,
       r118, r119, r120, r121, r122, r123, r124, r125, r126, r127, r128, r129, r130, r131, r210, r211, r212,
       r213, r214, r215, r216, r217, r218, r219, r220, r221, r222, r223, r224, r225, r226, r227, r228, r229,
       r230, r231, r310, r311, r312, r313, r314, r315, r316, r317, r318, r319, r320, r321, r322, r323, r324,
       r325, r326, r327, r328, r329, r330, r331;
  wire [31:0] o11, o12, o13, o14, o15, o16, o17, o18, o19, o21, o22, o23, o24, o25, o26, o27, o28, o29, o110,
       o111, o112, o113, o114, o115, o116, o117, o118, o119, o120, o121, o122, o123, o124, o125, o126, o127,
       o128, o129, o130, o131, o210, o211, o212, o213, o214, o215, o216, o217, o218, o219, o220, o221, o222,
       o223, o224, o225, o226, o227, o228, o229, o230, o231;

  Decoder #(.select(5), .disabled(0), .enable("false")) decoder_1 (
    .out0(r10), .out1(r11), .out2(r12), .out3(r13), .out4(r14), .out5(r15), .out6(r16), .out7(r17),
    .out8(r18), .out9(r19), .out10(r110), .out11(r111), .out12(r112), .out13(r113), .out14(r114),
    .out15(r115), .out16(r116), .out17(r117), .out18(r118), .out19(r119), .out20(r120), .out21(r121),
    .out22(r122), .out23(r123), .out24(r124), .out25(r125), .out26(r126), .out27(r127), .out28(r128),
    .out29(r129), .out30(r130), .out31(r131), .sel(A1));
  Decoder #(.select(5), .disabled(0), .enable("false")) decoder_2 (
    .out0(r20), .out1(r21), .out2(r22), .out3(r23), .out4(r24), .out5(r25), .out6(r26), .out7(r27),
    .out8(r28), .out9(r29), .out10(r210), .out11(r211), .out12(r212), .out13(r213), .out14(r214),
    .out15(r215), .out16(r216), .out17(r217), .out18(r218), .out19(r219), .out20(r220), .out21(r221),
    .out22(r222), .out23(r223), .out24(r224), .out25(r225), .out26(r226), .out27(r227), .out28(r228),
    .out29(r229), .out30(r230), .out31(r231), .sel(A2));
  Decoder #(.select(5), .disabled(0), .enable("false")) decoder_3 (
    .out0(r30), .out1(r31), .out2(r32), .out3(r33), .out4(r34), .out5(r35), .out6(r36), .out7(r37),
    .out8(r38), .out9(r39), .out10(r310), .out11(r311), .out12(r312), .out13(r313), .out14(r314),
    .out15(r315), .out16(r316), .out17(r317), .out18(r318), .out19(r319), .out20(r320), .out21(r321),
    .out22(r322), .out23(r323), .out24(r324), .out25(r325), .out26(r326), .out27(r327), .out28(r328),
    .out29(r329), .out30(r330), .out31(r331), .sel(WriteRegister));
  Multiplexer #(.select(5), .width(32), .disabled(0), .enable("false")) multiplexer_1 (
    .in0({32{1'b0}}), .in1(o11), .in2(o12), .in3(o13), .in4(o14), .in5(o15), .in6(o16), .in7(o17), .in8(o18),
    .in9(o19), .in10(o110), .in11(o111), .in12(o112), .in13(o113), .in14(o114), .in15(o115), .in16(o116),
    .in17(o117), .in18(o118), .in19(o119), .in20(o120), .in21(o121), .in22(o122), .in23(o123), .in24(o124),
    .in25(o125), .in26(o126), .in27(o127), .in28(o128), .in29(o129), .in30(o130), .in31(o131),
    .out(ReadData1), .sel(A1));
  Multiplexer #(.select(5), .width(32), .disabled(0), .enable("false")) multiplexer_2 (
    .in0({32{1'b0}}), .in1(o21), .in2(o22), .in3(o23), .in4(o24), .in5(o25), .in6(o26), .in7(o27), .in8(o28),
    .in9(o29), .in10(o210), .in11(o211), .in12(o212), .in13(o213), .in14(o214), .in15(o215), .in16(o216),
    .in17(o217), .in18(o218), .in19(o219), .in20(o220), .in21(o221), .in22(o222), .in23(o223), .in24(o224),
    .in25(o225), .in26(o226), .in27(o227), .in28(o228), .in29(o229), .in30(o230), .in31(o231),
    .out(ReadData2), .sel(A2));
  RegisterUnit registerunit_1 (
    .\input (WD), .c(in_4), .a3(r34), .we(in_5), .r(in_3), .in_5(r14), .in_6(r24), .o1(o14), .o2(o24));
  RegisterUnit registerunit_2 (
    .\input (WD), .c(in_4), .a3(r38), .we(in_5), .r(in_3), .in_5(r18), .in_6(r28), .o1(o18), .o2(o28));
  RegisterUnit registerunit_3 (
    .\input (WD), .c(in_4), .a3(r312), .we(in_5), .r(in_3), .in_5(r112), .in_6(r212), .o1(o112), .o2(o212));
  RegisterUnit registerunit_4 (
    .\input (WD), .c(in_4), .a3(r316), .we(in_5), .r(in_3), .in_5(r116), .in_6(r216), .o1(o116), .o2(o216));
  RegisterUnit registerunit_5 (
    .\input (WD), .c(in_4), .a3(r320), .we(in_5), .r(in_3), .in_5(r120), .in_6(r220), .o1(o120), .o2(o220));
  RegisterUnit registerunit_6 (
    .\input (WD), .c(in_4), .a3(r324), .we(in_5), .r(in_3), .in_5(r124), .in_6(r224), .o1(o124), .o2(o224));
  RegisterUnit registerunit_7 (
    .\input (WD), .c(in_4), .a3(r328), .we(in_5), .r(in_3), .in_5(r128), .in_6(r228), .o1(o128), .o2(o228));
  RegisterUnit registerunit_8 (
    .\input (WD), .c(in_4), .a3(r31), .we(in_5), .r(in_3), .in_5(r11), .in_6(r21), .o1(o11), .o2(o21));
  RegisterUnit registerunit_9 (
    .\input (WD), .c(in_4), .a3(r35), .we(in_5), .r(in_3), .in_5(r15), .in_6(r25), .o1(o15), .o2(o25));
  RegisterUnit registerunit_10 (
    .\input (WD), .c(in_4), .a3(r39), .we(in_5), .r(in_3), .in_5(r19), .in_6(r29), .o1(o19), .o2(o29));
  RegisterUnit registerunit_11 (
    .\input (WD), .c(in_4), .a3(r313), .we(in_5), .r(in_3), .in_5(r113), .in_6(r213), .o1(o113), .o2(o213));
  RegisterUnit registerunit_12 (
    .\input (WD), .c(in_4), .a3(r317), .we(in_5), .r(in_3), .in_5(r117), .in_6(r217), .o1(o117), .o2(o217));
  RegisterUnit registerunit_13 (
    .\input (WD), .c(in_4), .a3(r321), .we(in_5), .r(in_3), .in_5(r121), .in_6(r221), .o1(o121), .o2(o221));
  RegisterUnit registerunit_14 (
    .\input (WD), .c(in_4), .a3(r325), .we(in_5), .r(in_3), .in_5(r125), .in_6(r225), .o1(o125), .o2(o225));
  RegisterUnit registerunit_15 (
    .\input (WD), .c(in_4), .a3(r329), .we(in_5), .r(in_3), .in_5(r129), .in_6(r229), .o1(o129), .o2(o229));
  RegisterUnit registerunit_16 (
    .\input (WD), .c(in_4), .a3(r32), .we(in_5), .r(in_3), .in_5(r12), .in_6(r22), .o1(o12), .o2(o22));
  RegisterUnit registerunit_17 (
    .\input (WD), .c(in_4), .a3(r36), .we(in_5), .r(in_3), .in_5(r16), .in_6(r26), .o1(o16), .o2(o26));
  RegisterUnit registerunit_18 (
    .\input (WD), .c(in_4), .a3(r310), .we(in_5), .r(in_3), .in_5(r110), .in_6(r210), .o1(o110), .o2(o210));
  RegisterUnit registerunit_19 (
    .\input (WD), .c(in_4), .a3(r314), .we(in_5), .r(in_3), .in_5(r114), .in_6(r214), .o1(o114), .o2(o214));
  RegisterUnit registerunit_20 (
    .\input (WD), .c(in_4), .a3(r318), .we(in_5), .r(in_3), .in_5(r118), .in_6(r218), .o1(o118), .o2(o218));
  RegisterUnit registerunit_21 (
    .\input (WD), .c(in_4), .a3(r322), .we(in_5), .r(in_3), .in_5(r122), .in_6(r222), .o1(o122), .o2(o222));
  RegisterUnit registerunit_22 (
    .\input (WD), .c(in_4), .a3(r326), .we(in_5), .r(in_3), .in_5(r126), .in_6(r226), .o1(o126), .o2(o226));
  RegisterUnit registerunit_23 (
    .\input (WD), .c(in_4), .a3(r330), .we(in_5), .r(in_3), .in_5(r130), .in_6(r230), .o1(o130), .o2(o230));
  RegisterUnit registerunit_24 (
    .\input (WD), .c(in_4), .a3(r33), .we(in_5), .r(in_3), .in_5(r13), .in_6(r23), .o1(o13), .o2(o23));
  RegisterUnit registerunit_25 (
    .\input (WD), .c(in_4), .a3(r37), .we(in_5), .r(in_3), .in_5(r17), .in_6(r27), .o1(o17), .o2(o27));
  RegisterUnit registerunit_26 (
    .\input (WD), .c(in_4), .a3(r311), .we(in_5), .r(in_3), .in_5(r111), .in_6(r211), .o1(o111), .o2(o211));
  RegisterUnit registerunit_27 (
    .\input (WD), .c(in_4), .a3(r315), .we(in_5), .r(in_3), .in_5(r115), .in_6(r215), .o1(o115), .o2(o215));
  RegisterUnit registerunit_28 (
    .\input (WD), .c(in_4), .a3(r319), .we(in_5), .r(in_3), .in_5(r119), .in_6(r219), .o1(o119), .o2(o219));
  RegisterUnit registerunit_29 (
    .\input (WD), .c(in_4), .a3(r323), .we(in_5), .r(in_3), .in_5(r123), .in_6(r223), .o1(o123), .o2(o223));
  RegisterUnit registerunit_30 (
    .\input (WD), .c(in_4), .a3(r327), .we(in_5), .r(in_3), .in_5(r127), .in_6(r227), .o1(o127), .o2(o227));
  RegisterUnit registerunit_31 (
    .\input (WD), .c(in_4), .a3(r331), .we(in_5), .r(in_3), .in_5(r131), .in_6(r231), .o1(o131), .o2(o231));

  // Other names for the same wires on the sheet: clk = in_4; reset = in_3; WE = in_5
endmodule

module RegisterUnit (
  input  [31:0] \input ,
  input  a3,
  input  we,
  input  r,
  input  in_5,
  input  in_6,
  input  c,
  output [31:0] o1,
  output [31:0] o2
);

  wire [31:0] multiplexer_1_out, register_1_q;

  Multiplexer #(.width(32), .disabled(0), .enable("false")) multiplexer_1 (
    .in0(register_1_q), .in1(\input ), .out(multiplexer_1_out), .sel(a3));
  Register #(.width(32)) register_1 (.D(multiplexer_1_out), .en(we), .Q(register_1_q), .clk(c), .clr(r));
  Multiplexer #(.width(32), .disabled(0), .enable("false")) multiplexer_2 (
    .in1(register_1_q), .out(o1), .sel(in_5));  // open: in0
  Multiplexer #(.width(32), .disabled(0), .enable("false")) multiplexer_3 (
    .in1(register_1_q), .out(o2), .sel(in_6));  // open: in0
endmodule

module ALU (
  input  [31:0] A,
  input  [31:0] B,
  input  [3:0] Op,
  output [31:0] Result,
  output Zero
);

  wire [31:0] adder_1_out, and_1_out, or_1_out, subtractor_1_out;

  assign and_1_out = A & B;  // AND_Gate and_1, 32 bits wide
  assign or_1_out = A | B;  // OR_Gate or_1, 32 bits wide
  Adder #(.width(32)) adder_1 (.a(A), .b(B), .out(adder_1_out));  // open: cin, cout
  Subtractor #(.width(32)) subtractor_1 (.a(A), .b(B), .out(subtractor_1_out));  // open: bin, bout
  Multiplexer #(.select(4), .width(32), .enable("false")) multiplexer_1 (
    .in0(and_1_out), .in1(or_1_out), .in2(adder_1_out), .in6(subtractor_1_out), .in8({B[15:0], B[31:16]}),
    .out(Result), .sel(Op));  // open: in3, in4, in5, in7, in9, in10, in11, in12, in13, in14, in15
  Comparator #(.width(32), .mode("unsigned")) comparator_1 (.a(A), .b(B), .eq(Zero));  // open: gt, lt
endmodule
